// Logisim project mips-datapath-lab.circ as structural Verilog: 7 circuits, main circuit mips
module alu (
  input  [3:0] ALU_Control,
  input  [31:0] in_2,
  input  [31:0] in_3,
  output [31:0] out_4,
  output Zero
);

  wire comparator_1_lt;
  wire [31:0] adder_1_out, and_1_out, multiplexer_1_out, or_1_out, subtractor_1_out, xor_1_out;

  assign and_1_out = in_2 & in_3;  // AND_Gate and_1, 32 bits wide
  assign or_1_out = in_2 | in_3;  // OR_Gate or_1, 32 bits wide
  Adder #(.width(32)) adder_1 (.a(in_2), .b(in_3), .out(adder_1_out));  // open: cin, cout
  Subtractor #(.width(32)) subtractor_1 (.a(in_2), .b(in_3), .out(subtractor_1_out));  // open: bin, bout
  Comparator #(.width(32), .mode("unsigned")) comparator_1 (.a(in_2), .b(in_3), .lt(comparator_1_lt));  // open: gt, eq
  assign xor_1_out = in_2 ^ in_3;  // XOR_Gate xor_1, 32 bits wide
  Multiplexer #(.width(32), .enable("false")) multiplexer_1 (
    .in0({32{1'b0}}), .in1(32'h1), .out(multiplexer_1_out), .sel(comparator_1_lt));
  Multiplexer #(.select(4), .width(32), .disabled(0), .enable("false")) multiplexer_2 (
    .in0(and_1_out), .in1(or_1_out), .in2(adder_1_out), .in6(subtractor_1_out), .in7(multiplexer_1_out),
    .in12(xor_1_out), .out(out_4), .sel(ALU_Control));  // open: in3, in4, in5, in8, in9, in10, in11, in13, in14, in15
  Comparator #(.width(32), .mode("unsigned")) comparator_2 (.a(out_4), .b({32{1'b0}}), .eq(Zero));  // open: gt, lt

  // Notes on the sheet:
  //   A
  //   B
  //   Op selects the result
  //   Output
endmodule

module mips (
);

  wire clock_1_out, control_1_regwrite, Restart_Program_out, Zero_Reg_File_out;
  wire [1:0] undriven_6;
  wire [3:0] alu_control_1_operation;
  wire [4:0] undriven, undriven_2, undriven_3;
  wire [9:2] undriven_9;
  wire [15:0] undriven_5;
  wire [31:0] adder_1_out, bit_extender_1_out, PC_q, ram_1_data, rom_1_data, undriven_4, undriven_7,
       undriven_8, undriven_10;

  Register #(.width(32)) PC (.D(adder_1_out), .Q(PC_q), .clk(clock_1_out), .clr(Restart_Program_out));  // open: en
  Clock clock_1 (.out(clock_1_out));
  Button Restart_Program (.out(Restart_Program_out));
  Button Zero_Reg_File (.out(Zero_Reg_File_out));
  Adder #(.width(32)) adder_1 (.a(PC_q), .b(32'h4), .out(adder_1_out));  // open: cin, cout
  // Probe on rom_1_data
  ROM #(.dataWidth(32)) rom_1 (.addr(PC_q[9:2]), .data(rom_1_data));  // open: sel
  control control_1 (.RegWrite(control_1_regwrite));  // open: in_1, RegDst, Branch, MemRead, MemtoReg, ALUOp, MemWrite, ALUSrc
  // Probe on undriven_4
  reg_32 reg_32_1 (
    .ReadReg1(undriven_3), .ReadReg2(undriven), .WriteReg(undriven_2), .RegWrite(control_1_regwrite),
    .WriteData(undriven_4), .Clk(clock_1_out), .Reset(Zero_Reg_File_out));  // open: ReadData1, ReadData2
  // Probe on undriven_3
  // Probe on undriven
  // Probe on undriven_2
  assign bit_extender_1_out = {{16{undriven_5[15]}}, undriven_5};  // Bit_Extender bit_extender_1
  // Probe on bit_extender_1_out
  alu_control alu_control_1 (.Operation(alu_control_1_operation), .ALUOp(undriven_6));  // open: Func
  alu alu_1 (.in_2(undriven_7), .in_3(undriven_8));  // open: out_4, Zero, ALU_Control
  // Probe on undriven_7
  // Probe on undriven_8
  // Probe on alu_control_1_operation
  // Probe on adder_1_out
  // Probe on undriven_9
  RAM #(.dataWidth(32), .bus("separate")) ram_1 (
    .addr(undriven_9), .din(undriven_10), .data(ram_1_data), .clk(clock_1_out));  // open: str, sel, ld, clr

  // Notes on the sheet:
  //   Your name and date: 
  //   Clock
  //   Current Instruction
  //   contents of rom_1 (hex, n*v repeats v):
  //   8c090000 8c0a0004 8c08000c 12a5820 1696020 10a4022 1896825 18d702a 1148fffa
  //   Reg Write Data
  //   Imm. Value
  //   ALU Op
  //   Next PC
  //   Mem Addr
  //   Right-click and load the 1234.mem into the RAM.
endmodule

module instruction_type_decode (
  input  [5:0] opcode,
  output R_format,
  output lw,
  output sw,
  output beq
);

  Comparator #(.width(6), .mode("unsigned")) comparator_1 (.a({6{1'b0}}), .b(opcode));  // open: gt, eq, lt
  Comparator #(.width(6), .mode("unsigned")) comparator_2 (.b(opcode));  // open: a, gt, eq, lt
  Comparator #(.width(6), .mode("unsigned")) comparator_3 (.b(opcode));  // open: a, gt, eq, lt
  Comparator #(.width(6), .mode("unsigned")) comparator_4 (.b(opcode));  // open: a, gt, eq, lt

  // Notes on the sheet:
  //   This example sets "R-format" to true if opcode=00.
  //   Hint: Use comparators and a constant to check for the right values
endmodule

module control_decode (
  input  Rformat,
  input  lw,
  input  sw,
  input  beq,
  output RegDst,
  output ALUSrc,
  output MemtoReg,
  output RegWrite,
  output MemRead,
  output MemWrite,
  output Branch,
  output ALUOp1,
  output ALUOp0
);

  // OR_Gate or_1 has open pins: out=lw
  // OR_Gate or_2 has open pins: out=lw

  assign ALUOp0 = beq;
  assign ALUOp1 = lw;
  assign Branch = beq;
  assign MemRead = lw;
  assign MemtoReg = lw;
  assign MemWrite = lw;
  assign RegDst = lw;
  assign RegWrite = lw;
  assign Rformat = lw;
  assign sw = lw;

  // Notes on the sheet:
  //   Use the Combinational Analysis
  //   Tool to generate this
  //   logic and then copy/paste
  //   it into here.
endmodule

module alu_control (
  input  [5:0] Func,
  input  [1:0] ALUOp,
  output [3:0] Operation
);

  wire not_1_out, undriven, undriven_2, undriven_3;

  not not_1 (not_1_out, undriven);
  not not_2 (not_1_out, not_1_out);
  // NOT_Gate not_3 has open pins: in=open, out=not_1_out
  not not_4 (not_1_out, not_1_out);
  not not_5 (not_1_out, not_1_out);
  // AND_Gate and_1 is placed but not wired
  // AND_Gate and_2 is placed but not wired
  // AND_Gate and_3 is placed but not wired
  // AND_Gate and_4 is placed but not wired
  // AND_Gate and_5 has open pins: in5=undriven_2, out=open
  // AND_Gate and_6 has open pins: in0=undriven_2, in5=undriven_3, out=open
  // AND_Gate and_7 has open pins: in0=undriven_3, out=open
  not not_6 (not_1_out, not_1_out);
  // OR_Gate or_1 has open pins: out=not_1_out
  // OR_Gate or_2 has open pins: out=not_1_out
  // OR_Gate or_3 has open pins: out=not_1_out
  // OR_Gate or_4 has open pins: out=not_1_out
  // OR_Gate or_5 has open pins: out=not_1_out

  // Notes on the sheet:
  //   Inputs
  //   ALUOp
  //   Function
  //   B -- OR
  //   Hint: Here is the logic for the first row: 
  //   A -- if (ALUOp1=0 and ALUOp0=0)
  //   D -- then output = 2 = 0010
  //   A
  //   C
  //   C -- if (ALUOp1=1 and ALUOp0=0 and F3, F2, F1, F0 are all 0)
  //   B
  //   True for 0010=2
  //   True for 0110=6
  //   True for 0001=1
  //   True for 0111=7
  //   True for 0000=0
  //   We have 5 possible outputs
  //   D
  //   Depending on which input is 1,
  //   one of the outputs above will be selected.
endmodule

module control (
  input  [5:0] in_1,
  output RegDst,
  output Branch,
  output MemRead,
  output MemtoReg,
  output [1:0] ALUOp,
  output MemWrite,
  output ALUSrc,
  output RegWrite
);

  wire control_decode_1_p1, control_decode_1_p3, control_decode_1_p8, control_decode_1_p9;

  instruction_type_decode instruction_type_decode_1 ();  // open: opcode, R_format, lw, sw, beq
  // control_decode control_decode_1: pin names not known; wires that end beside it: control_decode_1_p1, MemWrite, control_decode_1_p3, ALUSrc, RegWrite, control_decode_1_p1, MemRead, control_decode_1_p8, control_decode_1_p9

  // Notes on the sheet:
  //   Instruction OpCode
  //   Decode the Instruction Type first
  //   From the Insturction Type,
  //   decode the control signals
endmodule

module reg_32 (
  input  [4:0] ReadReg1,
  input  [4:0] ReadReg2,
  input  [4:0] WriteReg,
  input  RegWrite,
  input  [31:0] WriteData,
  input  Clk,
  input  Reset,
  output [31:0] ReadData1,
  output [31:0] ReadData2
);

  wire decoder_1_out0, decoder_1_out1, decoder_2_out0, decoder_2_out1, decoder_2_out2, decoder_2_out3,
       decoder_3_out0, decoder_3_out1, decoder_3_out2, decoder_3_out3, decoder_4_out0, decoder_4_out1,
       decoder_4_out2, decoder_4_out3, decoder_5_out0, decoder_5_out1, decoder_5_out2, decoder_5_out3,
       decoder_6_out0, decoder_6_out1, decoder_6_out2, decoder_6_out3, decoder_7_out0, decoder_7_out1,
       decoder_7_out2, decoder_7_out3, decoder_8_out0, decoder_8_out1, decoder_8_out2, decoder_8_out3,
       decoder_9_out0, decoder_9_out1, decoder_9_out2, decoder_9_out3, decoder_10_out0, decoder_10_out1,
       decoder_10_out2, decoder_10_out3, decoder_11_out0, decoder_11_out1, decoder_11_out2, decoder_11_out3;
  wire [31:0] multiplexer_1_out, multiplexer_2_out, multiplexer_3_out, multiplexer_4_out, multiplexer_5_out,
       multiplexer_6_out, multiplexer_7_out, multiplexer_8_out, multiplexer_9_out, multiplexer_10_out,
       multiplexer_13_out, multiplexer_14_out, multiplexer_15_out, multiplexer_16_out, multiplexer_17_out,
       multiplexer_18_out, multiplexer_19_out, multiplexer_20_out, multiplexer_21_out, multiplexer_22_out,
       register_1_q, register_2_q, register_3_q, register_4_q, register_5_q, register_6_q, register_7_q,
       register_8_q, register_9_q, register_10_q, register_11_q, register_12_q, register_13_q, register_14_q,
       register_15_q, register_16_q, register_17_q, register_18_q, register_19_q, register_20_q,
       register_21_q, register_22_q, register_23_q, register_24_q, register_25_q, register_26_q,
       register_27_q, register_28_q, register_29_q, register_30_q, register_31_q;

  // Probe on WriteReg
  Decoder #(.disabled(0)) decoder_1 (.out0(decoder_1_out0), .out1(decoder_1_out1), .sel(WriteReg[4]), .en(RegWrite));
  Decoder #(.select(2), .disabled(0)) decoder_2 (
    .out0(decoder_2_out0), .out1(decoder_2_out1), .out2(decoder_2_out2), .out3(decoder_2_out3),
    .sel(WriteReg[3:2]), .en(decoder_1_out0));
  Decoder #(.select(2), .disabled(0)) decoder_3 (
    .out0(decoder_3_out0), .out1(decoder_3_out1), .out2(decoder_3_out2), .out3(decoder_3_out3),
    .sel(WriteReg[1:0]), .en(decoder_2_out0));
  Decoder #(.select(2), .disabled(0)) decoder_4 (
    .out0(decoder_4_out0), .out1(decoder_4_out1), .out2(decoder_4_out2), .out3(decoder_4_out3),
    .sel(WriteReg[1:0]), .en(decoder_2_out1));
  Decoder #(.select(2), .disabled(0)) decoder_5 (
    .out0(decoder_5_out0), .out1(decoder_5_out1), .out2(decoder_5_out2), .out3(decoder_5_out3),
    .sel(WriteReg[1:0]), .en(decoder_2_out2));
  Decoder #(.select(2), .disabled(0)) decoder_6 (
    .out0(decoder_6_out0), .out1(decoder_6_out1), .out2(decoder_6_out2), .out3(decoder_6_out3),
    .sel(WriteReg[1:0]), .en(decoder_2_out3));
  Register #(.width(32)) register_1 (.D(WriteData), .en(decoder_3_out1), .Q(register_1_q), .clk(Clk), .clr(Reset));
  Register #(.width(32)) register_2 (.D(WriteData), .en(decoder_3_out2), .Q(register_2_q), .clk(Clk), .clr(Reset));
  Register #(.width(32)) register_3 (.D(WriteData), .en(decoder_3_out3), .Q(register_3_q), .clk(Clk), .clr(Reset));
  Register #(.width(32)) register_4 (.D(WriteData), .en(decoder_4_out0), .Q(register_4_q), .clk(Clk), .clr(Reset));
  Register #(.width(32)) register_5 (.D(WriteData), .en(decoder_4_out1), .Q(register_5_q), .clk(Clk), .clr(Reset));
  Register #(.width(32)) register_6 (.D(WriteData), .en(decoder_4_out2), .Q(register_6_q), .clk(Clk), .clr(Reset));
  Register #(.width(32)) register_7 (.D(WriteData), .en(decoder_4_out3), .Q(register_7_q), .clk(Clk), .clr(Reset));
  Register #(.width(32)) register_8 (.D(WriteData), .en(decoder_5_out0), .Q(register_8_q), .clk(Clk), .clr(Reset));
  Register #(.width(32)) register_9 (.D(WriteData), .en(decoder_5_out1), .Q(register_9_q), .clk(Clk), .clr(Reset));
  Register #(.width(32)) register_10 (.D(WriteData), .en(decoder_5_out2), .Q(register_10_q), .clk(Clk), .clr(Reset));
  Register #(.width(32)) register_11 (.D(WriteData), .en(decoder_5_out3), .Q(register_11_q), .clk(Clk), .clr(Reset));
  Register #(.width(32)) register_12 (.D(WriteData), .en(decoder_6_out0), .Q(register_12_q), .clk(Clk), .clr(Reset));
  Register #(.width(32)) register_13 (.D(WriteData), .en(decoder_6_out1), .Q(register_13_q), .clk(Clk), .clr(Reset));
  Register #(.width(32)) register_14 (.D(WriteData), .en(decoder_6_out2), .Q(register_14_q), .clk(Clk), .clr(Reset));
  Register #(.width(32)) register_15 (.D(WriteData), .en(decoder_6_out3), .Q(register_15_q), .clk(Clk), .clr(Reset));
  // Probe on {32{1'b0}}
  // Probe on register_1_q
  // Probe on register_2_q
  // Probe on register_3_q
  // Probe on register_4_q
  // Probe on register_5_q
  // Probe on register_6_q
  // Probe on register_7_q
  // Probe on register_8_q
  // Probe on register_9_q
  // Probe on register_10_q
  // Probe on register_11_q
  // Probe on register_12_q
  // Probe on register_13_q
  // Probe on register_14_q
  // Probe on register_15_q
  // Probe on ReadReg1
  Multiplexer #(.select(2), .width(32), .enable("false")) multiplexer_1 (
    .in0({32{1'b0}}), .in1(register_1_q), .in2(register_2_q), .in3(register_3_q), .out(multiplexer_1_out),
    .sel(ReadReg1[1:0]));
  Multiplexer #(.select(2), .width(32), .enable("false")) multiplexer_2 (
    .in0(register_4_q), .in1(register_5_q), .in2(register_6_q), .in3(register_7_q), .out(multiplexer_2_out),
    .sel(ReadReg1[1:0]));
  Multiplexer #(.select(2), .width(32), .enable("false")) multiplexer_3 (
    .in0(register_8_q), .in1(register_9_q), .in2(register_10_q), .in3(register_11_q),
    .out(multiplexer_3_out), .sel(ReadReg1[1:0]));
  Multiplexer #(.select(2), .width(32), .enable("false")) multiplexer_4 (
    .in0(register_12_q), .in1(register_13_q), .in2(register_14_q), .in3(register_15_q),
    .out(multiplexer_4_out), .sel(ReadReg1[1:0]));
  // Probe on ReadReg2
  Multiplexer #(.select(2), .width(32), .enable("false")) multiplexer_5 (
    .in0({32{1'b0}}), .in1(register_1_q), .in2(register_2_q), .in3(register_3_q), .out(multiplexer_5_out),
    .sel(ReadReg2[1:0]));
  Multiplexer #(.select(2), .width(32), .enable("false")) multiplexer_6 (
    .in0(register_4_q), .in1(register_5_q), .in2(register_6_q), .in3(register_7_q), .out(multiplexer_6_out),
    .sel(ReadReg2[1:0]));
  Multiplexer #(.select(2), .width(32), .enable("false")) multiplexer_7 (
    .in0(register_8_q), .in1(register_9_q), .in2(register_10_q), .in3(register_11_q),
    .out(multiplexer_7_out), .sel(ReadReg2[1:0]));
  Multiplexer #(.select(2), .width(32), .enable("false")) multiplexer_8 (
    .in0(register_12_q), .in1(register_13_q), .in2(register_14_q), .in3(register_15_q),
    .out(multiplexer_8_out), .sel(ReadReg2[1:0]));
  Multiplexer #(.select(2), .width(32), .enable("false")) multiplexer_9 (
    .in0(multiplexer_5_out), .in1(multiplexer_6_out), .in2(multiplexer_7_out), .in3(multiplexer_8_out),
    .out(multiplexer_9_out), .sel(ReadReg2[3:2]));
  Multiplexer #(.select(2), .width(32), .enable("false")) multiplexer_10 (
    .in0(multiplexer_1_out), .in1(multiplexer_2_out), .in2(multiplexer_3_out), .in3(multiplexer_4_out),
    .out(multiplexer_10_out), .sel(ReadReg1[3:2]));
  Decoder #(.select(2), .disabled(0)) decoder_7 (
    .out0(decoder_7_out0), .out1(decoder_7_out1), .out2(decoder_7_out2), .out3(decoder_7_out3),
    .sel(WriteReg[3:2]), .en(decoder_1_out1));
  Decoder #(.select(2), .disabled(0)) decoder_8 (
    .out0(decoder_8_out0), .out1(decoder_8_out1), .out2(decoder_8_out2), .out3(decoder_8_out3),
    .sel(WriteReg[1:0]), .en(decoder_7_out0));
  Decoder #(.select(2), .disabled(0)) decoder_9 (
    .out0(decoder_9_out0), .out1(decoder_9_out1), .out2(decoder_9_out2), .out3(decoder_9_out3),
    .sel(WriteReg[1:0]), .en(decoder_7_out1));
  Decoder #(.select(2), .disabled(0)) decoder_10 (
    .out0(decoder_10_out0), .out1(decoder_10_out1), .out2(decoder_10_out2), .out3(decoder_10_out3),
    .sel(WriteReg[1:0]), .en(decoder_7_out2));
  Decoder #(.select(2), .disabled(0)) decoder_11 (
    .out0(decoder_11_out0), .out1(decoder_11_out1), .out2(decoder_11_out2), .out3(decoder_11_out3),
    .sel(WriteReg[1:0]), .en(decoder_7_out3));
  Register #(.width(32)) register_16 (.D(WriteData), .en(decoder_8_out0), .Q(register_16_q), .clk(Clk), .clr(Reset));
  Register #(.width(32)) register_17 (.D(WriteData), .en(decoder_8_out1), .Q(register_17_q), .clk(Clk), .clr(Reset));
  Register #(.width(32)) register_18 (.D(WriteData), .en(decoder_8_out2), .Q(register_18_q), .clk(Clk), .clr(Reset));
  Register #(.width(32)) register_19 (.D(WriteData), .en(decoder_8_out3), .Q(register_19_q), .clk(Clk), .clr(Reset));
  Register #(.width(32)) register_20 (.D(WriteData), .en(decoder_9_out0), .Q(register_20_q), .clk(Clk), .clr(Reset));
  Register #(.width(32)) register_21 (.D(WriteData), .en(decoder_9_out1), .Q(register_21_q), .clk(Clk), .clr(Reset));
  Register #(.width(32)) register_22 (.D(WriteData), .en(decoder_9_out2), .Q(register_22_q), .clk(Clk), .clr(Reset));
  Register #(.width(32)) register_23 (.D(WriteData), .en(decoder_9_out3), .Q(register_23_q), .clk(Clk), .clr(Reset));
  Register #(.width(32)) register_24 (.D(WriteData), .en(decoder_10_out0), .Q(register_24_q), .clk(Clk), .clr(Reset));
  Register #(.width(32)) register_25 (.D(WriteData), .en(decoder_10_out1), .Q(register_25_q), .clk(Clk), .clr(Reset));
  Register #(.width(32)) register_26 (.D(WriteData), .en(decoder_10_out2), .Q(register_26_q), .clk(Clk), .clr(Reset));
  Register #(.width(32)) register_27 (.D(WriteData), .en(decoder_10_out3), .Q(register_27_q), .clk(Clk), .clr(Reset));
  Register #(.width(32)) register_28 (.D(WriteData), .en(decoder_11_out0), .Q(register_28_q), .clk(Clk), .clr(Reset));
  Register #(.width(32)) register_29 (.D(WriteData), .en(decoder_11_out1), .Q(register_29_q), .clk(Clk), .clr(Reset));
  Register #(.width(32)) register_30 (.D(WriteData), .en(decoder_11_out2), .Q(register_30_q), .clk(Clk), .clr(Reset));
  Register #(.width(32)) register_31 (.D(WriteData), .en(decoder_11_out3), .Q(register_31_q), .clk(Clk), .clr(Reset));
  // Probe on register_16_q
  // Probe on register_17_q
  // Probe on register_18_q
  // Probe on register_19_q
  // Probe on register_20_q
  // Probe on register_21_q
  // Probe on register_22_q
  // Probe on register_23_q
  // Probe on register_24_q
  // Probe on register_25_q
  // Probe on register_26_q
  // Probe on register_27_q
  // Probe on register_28_q
  // Probe on register_29_q
  // Probe on register_30_q
  // Probe on register_31_q
  Multiplexer #(.width(32), .enable("false")) multiplexer_11 (
    .in0(multiplexer_10_out), .in1(multiplexer_21_out), .out(ReadData1), .sel(ReadReg1[4]));
  Multiplexer #(.width(32), .enable("false")) multiplexer_12 (
    .in0(multiplexer_9_out), .in1(multiplexer_22_out), .out(ReadData2), .sel(ReadReg2[4]));
  Multiplexer #(.select(2), .width(32), .enable("false")) multiplexer_13 (
    .in0(register_16_q), .in1(register_17_q), .in2(register_18_q), .in3(register_19_q),
    .out(multiplexer_13_out), .sel(ReadReg1[1:0]));
  Multiplexer #(.select(2), .width(32), .enable("false")) multiplexer_14 (
    .in0(register_20_q), .in1(register_21_q), .in2(register_22_q), .in3(register_23_q),
    .out(multiplexer_14_out), .sel(ReadReg1[1:0]));
  Multiplexer #(.select(2), .width(32), .enable("false")) multiplexer_15 (
    .in0(register_24_q), .in1(register_25_q), .in2(register_26_q), .in3(register_27_q),
    .out(multiplexer_15_out), .sel(ReadReg1[1:0]));
  Multiplexer #(.select(2), .width(32), .enable("false")) multiplexer_16 (
    .in0(register_28_q), .in1(register_29_q), .in2(register_30_q), .in3(register_31_q),
    .out(multiplexer_16_out), .sel(ReadReg1[1:0]));
  Multiplexer #(.select(2), .width(32), .enable("false")) multiplexer_17 (
    .in0(register_16_q), .in1(register_17_q), .in2(register_18_q), .in3(register_19_q),
    .out(multiplexer_17_out), .sel(ReadReg2[1:0]));
  Multiplexer #(.select(2), .width(32), .enable("false")) multiplexer_18 (
    .in0(register_20_q), .in1(register_21_q), .in2(register_22_q), .in3(register_23_q),
    .out(multiplexer_18_out), .sel(ReadReg2[1:0]));
  Multiplexer #(.select(2), .width(32), .enable("false")) multiplexer_19 (
    .in0(register_24_q), .in1(register_25_q), .in2(register_26_q), .in3(register_27_q),
    .out(multiplexer_19_out), .sel(ReadReg2[1:0]));
  Multiplexer #(.select(2), .width(32), .enable("false")) multiplexer_20 (
    .in0(register_28_q), .in1(register_29_q), .in2(register_30_q), .in3(register_31_q),
    .out(multiplexer_20_out), .sel(ReadReg2[1:0]));
  Multiplexer #(.select(2), .width(32), .enable("false")) multiplexer_21 (
    .in0(multiplexer_17_out), .in1(multiplexer_18_out), .in2(multiplexer_19_out), .in3(multiplexer_20_out),
    .out(multiplexer_21_out), .sel(ReadReg2[3:2]));
  Multiplexer #(.select(2), .width(32), .enable("false")) multiplexer_22 (
    .in0(multiplexer_13_out), .in1(multiplexer_14_out), .in2(multiplexer_15_out), .in3(multiplexer_16_out),
    .out(multiplexer_22_out), .sel(ReadReg1[3:2]));
endmodule
